# Fritzing sketch AVR_Radio (saved by Fritzing 0.9.3b)
breadboards: 1

parts:
  Part1 = Arduino Uno (Rev3)
  S1 = Momentary Switch [package=ksa_sealed_tac_switch]
  S2 = Momentary Switch [package=ksa_sealed_tac_switch]
  S3 = Momentary Switch [package=ksa_sealed_tac_switch]
  LCD1 = LCD screen
  J1 = female pin header, 15 pins [form="♀ (female)"]
  R1 = Resistor [tolerance=±5% resistance=1k package=THT]
  SP1 = SPEAKER [package=pcb_mount_speaker]  # not connected
  SP2 = SPEAKER [package=pcb_mount_speaker]  # not connected

nets:
  N1: Part1.A0, J1.pin1
  N2: Part1.A1, J1.pin4
  N3: Part1.A2, J1.pin3
  N4: Part1.A3, J1.pin2
  N5: Part1.A4/SDA, J1.pin14
  N6: Part1.A5/SCL, J1.pin15
  N7: Part1.D8, S3.3, S3.4
  N8: Part1.D9_PWM, S2.3, S2.4
  N9: Part1.D10_PWM/SS, S1.3, S1.4
  N10: Part1.D2, LCD1.RS
  N11: Part1.D3_PWM, LCD1.E
  N12: Part1.D4, LCD1.DB4
  N13: Part1.D5_PWM, LCD1.DB5
  N14: Part1.D6_PWM, LCD1.DB6
  N15: Part1.D7, LCD1.DB7
  5V: Part1.5V, LCD1.VDD, J1.pin7
  GND: Part1.GND, S1.1, S1.2, S2.1, S2.2, S3.1, S3.2, LCD1.VSS, LCD1.R/W, LCD1.LED-, J1.pin5, R1.Pin_0
  N16: LCD1.LED+, R1.Pin_1

notes:
  +12 V
  Left Out
  Right Out
  1
  15
  Up   Down   Scan
